# Fritzing sketch Litar Kawal Servo Motor dan LED Menggunakan Rotary Encoder (saved by Fritzing 0.9.2b)
breadboards: 1

parts:
  RE1 = KY-040 Rotary encoder [package=THT]
  Part1 = Arduino Uno (Rev3) - ICSP
  R1 = Resistor [tolerance=±5% resistance=220 package="2010 [SMD]"]
  LED2 = smd LED [color="Red (633nm)" package="0805 [SMD]"]
  J1 = Basic Servo

nets:
  GND: RE1.GND, Part1.GND, LED2.cathode, J1.gnd
  VCC: RE1.Vcc, Part1.5V, J1.vcc
  N1: RE1.SW, Part1.D11_PWM/MOSI
  N2: RE1.DT, Part1.D3_PWM
  N3: RE1.CLK, Part1.D2
  N4: Part1.D8, J1.pulse
  N5: Part1.D4, R1.Pin_0
  N6: R1.Pin_1, LED2.anode

custom parts:
  KY-040 Rotary encoder: KY-040 Rotary Encoder with switch on breakout borad from AZ Delivery
